# Fritzing sketch esp32_bme680_sketch (saved by Fritzing 0.9.3b)

parts:
  U1 = ESP32-38PinWide [part_number=ESP32-38PinWide]
  Part1 = Adafruit BME680

nets:
  N1: U1.3.3, Part1.VIN
  N2: U1.GPIO16, Part1.SDI/SDA
  N3: U1.GPIO17, Part1.SCK/SCL
  GND: U1.GND, Part1.GND

custom parts:
  ESP32-38PinWide: Generic 38-Pin ESP32 with wide format (only access to one side of pins on a breadboard) based on Stephen Lilley's HiLetgo ESP-WROOM-32 ESP32 ESP-32S Development Board.
